# Fritzing sketch simpleinfrared (saved by Fritzing 0.8.5b)
breadboards: 1

parts:
  IR1 = TSOP312.., 314.. [package=THT]
  LED1 = LED - 5mm [color="Red (633nm)" package="5 mm [THT]"]
  Bauteil1 = Arduino Uno (Rev3)
  R1 = Resistor [tolerance=±5% resistance=2.2k package=THT]

nets:
  N1: IR1.GND, Bauteil1.D3_PWM
  N2: IR1.Vs, LED1.cathode, Bauteil1.GND
  N3: IR1.Data, Bauteil1.5V, R1.Pin_0, R1.Pin_1
  N4: LED1.anode, Bauteil1.D13/SCK

notes:
  /**
  * based on this
  * http://playground.arduino.cc/Main/PanasonicIrSensor
  * use with some IR remote control
  *
  *
  *
  */
  int ledpin = 3; // this is just for reference
  int irsensorpin = 2; // read digital
  void setup(){
  Serial.begin(9600);// for seeing whats going on
  pinMode(ledpin, OUTPUT); // init
  pinMode(irsensorpin, INPUT); // init
  }
  void loop(){
  int recieved = digitalRead(irsensorpin); // read from the pin
  /**
  * if there is something it is 0
  * if not it is 1
  */
  if(recieved == 0){
  digitalWrite(ledpin, HIGH);// torn the LED on
  Serial.println("Message recieved");
  }else{
  digitalWrite(ledpin, LOW);// turn the LED off
  }
  delay(10);// wait a bit
  }
