# Fritzing sketch pushbutton (saved by Fritzing 0.8.3b)
breadboards: 1

parts:
  Bauteil1 = Arduino Uno (Rev3)
  S1 = Pushbutton [package=THT]
  R1 = Resistor [tolerance=±5% resistance=10k package=THT]
  LED1 = LED - 5mm [color="Red (633nm)" package="5 mm [THT]"]
  R2 = Resistor [tolerance=±5% resistance=220 package=THT]

nets:
  N1: Bauteil1.ICSP_SCK, Bauteil1.D13/SCK, R2.Pin_1
  N2: Bauteil1.GND, R1.Pin_1, LED1.cathode
  N3: Bauteil1.D2, S1.leg0, R1.Pin_0
  N4: Bauteil1.5V, S1.leg1
  N5: LED1.anode, R2.Pin_0
