# Fritzing sketch relay (saved by Fritzing 0.8.5b)
breadboards: 1

parts:
  Bauteil1 = Arduino Uno (Rev3)
  R1 = Resistor [tolerance=±5% resistance=220 package=THT]
  LED1 = LED - 5mm [color="Red (633nm)" package="5 mm [THT]"]
  U1 = RELAY-2 [package=relay-g5v]
  VCC1 = 4 x AAA Battery Mount

nets:
  N1: Bauteil1.D13/SCK, U1.2
  N2: Bauteil1.GND, U1.9
  N3: R1.Pin_0, LED1.anode
  N4: R1.Pin_1, VCC1.+
  N5: LED1.cathode, U1.1
  N6: U1.10, VCC1.-
